// Logisim project logisim_stack.circ as structural Verilog: 26 circuits, main circuit main
module main (
  input  CLK,
  input  RESET,
  input  [1:0] COMMAND,
  input  [2:0] INDEX,
  input  [3:0] IO_DATA_in,
  output [3:0] IO_DATA_out
);

  wire [3:0] stack_1_d0, stack_1_d1, stack_1_d2, stack_1_d3, stack_1_d4;

  // Probe on stack_1_d0
  stack stack_1 (
    .CLK(CLK), .RESET(RESET), .COMMAND(COMMAND), .INDEX(INDEX), .IO_DATA_in(IO_DATA_in), .d0(stack_1_d0),
    .d1(stack_1_d1), .d2(stack_1_d2), .d3(stack_1_d3), .d4(stack_1_d4), .IO_DATA_out(IO_DATA_out));
  // Probe on stack_1_d1
  // Probe on stack_1_d2
  // Probe on stack_1_d3
  // Probe on stack_1_d4
endmodule

module rs_trigger (
  input  r,
  input  s,
  output q,
  output neg_q
);

  wire nor_2_out, por_1_out;

  nor nor_1 (q, r, neg_q);
  nor nor_2 (nor_2_out, q, s);
  POR por_1 (.out(por_1_out));
  or or_1 (neg_q, nor_2_out, por_1_out);
endmodule

module rs_sync_trigger (
  input  r,
  input  c,
  input  s,
  output q,
  output neg_q
);

  wire and_1_out, and_2_out;

  and and_1 (and_1_out, r, c);
  and and_2 (and_2_out, c, s);
  rs_trigger rs_trigger_1 (.r(and_1_out), .s(and_2_out), .q(q), .neg_q(neg_q));
endmodule

module d_trigger (
  input  d,
  input  c,
  output q,
  output neg_q
);

  wire not_1_out;

  not not_1 (not_1_out, d);
  rs_sync_trigger rs_sync_trigger_1 (.r(not_1_out), .c(c), .s(d), .q(q), .neg_q(neg_q));
endmodule

module d_4_bits_trigger (
  input  reset,
  input  sync,
  input  [3:0] d,
  output [3:0] q
);

  wire d0, d1, d2, d3, d_trigger_1_neg_q, d_trigger_2_neg_q, d_trigger_3_neg_q, d_trigger_4_neg_q, not_1_out,
       SYNC_t;
  wire [3:0] bit_extender_1_out;

  assign bit_extender_1_out = {{3{not_1_out}}, not_1_out};  // Bit_Extender bit_extender_1
  not not_1 (not_1_out, reset);
  assign {d3, d2, d1, d0} = bit_extender_1_out & d;  // AND_Gate and_1, 4 bits wide
  or or_1 (SYNC_t, reset, sync);
  d_trigger d_trigger_1 (.d(d0), .c(SYNC_t), .q(q[0]), .neg_q(d_trigger_1_neg_q));
  d_trigger d_trigger_2 (.d(d1), .c(SYNC_t), .q(q[1]), .neg_q(d_trigger_2_neg_q));
  d_trigger d_trigger_3 (.d(d2), .c(SYNC_t), .q(q[2]), .neg_q(d_trigger_3_neg_q));
  d_trigger d_trigger_4 (.d(d3), .c(SYNC_t), .q(q[3]), .neg_q(d_trigger_4_neg_q));
endmodule

module dec_3_to_8 (
  input  [2:0] in_1,
  output [7:0] out_2
);

  wire not_1_out, not_2_out, not_3_out, not_4_out, not_5_out, not_6_out, not_7_out, not_8_out, not_9_out,
       not_10_out, not_11_out, not_12_out;

  not not_1 (not_1_out, in_1[0]);
  not not_2 (not_2_out, in_1[1]);
  and and_1 (out_2[0], not_1_out, not_2_out, not_3_out);
  not not_3 (not_3_out, in_1[2]);
  not not_4 (not_4_out, in_1[1]);
  and and_2 (out_2[1], in_1[0], not_4_out, not_5_out);
  not not_5 (not_5_out, in_1[2]);
  not not_6 (not_6_out, in_1[0]);
  and and_3 (out_2[2], not_6_out, in_1[1], not_7_out);
  not not_7 (not_7_out, in_1[2]);
  and and_4 (out_2[3], in_1[0], in_1[1], not_8_out);
  not not_8 (not_8_out, in_1[2]);
  not not_9 (not_9_out, in_1[0]);
  not not_10 (not_10_out, in_1[1]);
  and and_5 (out_2[4], not_9_out, not_10_out, in_1[2]);
  not not_11 (not_11_out, in_1[1]);
  and and_6 (out_2[5], in_1[0], not_11_out, in_1[2]);
  not not_12 (not_12_out, in_1[0]);
  and and_7 (out_2[6], not_12_out, in_1[1], in_1[2]);
  and and_8 (out_2[7], in_1[0], in_1[1], in_1[2]);
endmodule

module d_3_bits_trigger (
  input  reset,
  input  sync,
  input  [2:0] d,
  output [2:0] q
);

  wire [3:3] d_4_bits_trigger_1_q;

  d_4_bits_trigger d_4_bits_trigger_1 (.reset(reset), .sync(sync), .d({1'b0, d}), .q({d_4_bits_trigger_1_q[3], q}));
  // also tied to GND on the sheet: d_4_bits_trigger_1_q[3]
endmodule

module current_index (
  input  reset,
  input  [1:0] cmd,
  input  sync,
  output [2:0] index
);

  wire not_1_out;
  wire [2:0] d_3_bits_trigger_1_q, d_3_bits_trigger_2_q;

  next_index next_index_1 (.cmd(cmd), .sync(sync), .index(d_3_bits_trigger_2_q), .next_idx(index));
  d_3_bits_trigger d_3_bits_trigger_1 (.reset(reset), .sync(sync), .d(index), .q(d_3_bits_trigger_1_q));
  not not_1 (not_1_out, sync);
  d_3_bits_trigger d_3_bits_trigger_2 (
    .reset(reset), .sync(not_1_out), .d(d_3_bits_trigger_1_q), .q(d_3_bits_trigger_2_q));

  // Other names for the same wires on the sheet: NEXT_IDX[2:0] = index
endmodule

module plus_3_bits (
  input  [2:0] in_1,
  input  [2:0] in_2,
  output [2:0] q,
  output c
);

  wire plus_2_bits_1_c;

  plus_2_bits plus_2_bits_1 (
    .n0(in_1[0]), .n1(in_1[1]), .m0(in_2[0]), .m1(in_2[1]), .s0(q[0]), .s1(q[1]), .c(plus_2_bits_1_c));
  plus3 plus3_1 (.in_1(plus_2_bits_1_c), .in_2(in_1[2]), .in_3(in_2[2]), .s(q[2]), .c(c));
endmodule

module plus2 (
  input  in_1,
  input  in_2,
  output s,
  output c
);

  xor xor_1 (s, in_1, in_2);
  and and_1 (c, in_1, in_2);
endmodule

module plus3 (
  input  in_1,
  input  in_2,
  input  in_3,
  output s,
  output c
);

  wire plus2_1_c, plus2_1_s, plus2_2_c;

  plus2 plus2_1 (.in_1(in_2), .in_2(in_3), .s(plus2_1_s), .c(plus2_1_c));
  plus2 plus2_2 (.in_1(in_1), .in_2(plus2_1_s), .s(s), .c(plus2_2_c));
  or or_1 (c, plus2_2_c, plus2_1_c);
endmodule

module plus_2_bits (
  input  n0,
  input  n1,
  input  m0,
  input  m1,
  output s0,
  output s1,
  output c
);

  wire plus2_1_c;

  plus2 plus2_1 (.in_1(n0), .in_2(m0), .s(s0), .c(plus2_1_c));
  plus3 plus3_1 (.in_1(plus2_1_c), .in_2(n1), .in_3(m1), .s(s1), .c(c));
endmodule

module plus_3_bits_mod_5 (
  input  [2:0] in_1,
  input  [2:0] in_2,
  output [2:0] out_3
);

  wire [2:0] plus_3_bits_1_q;
  wire [3:3] plus_3_bits_1_c;

  plus_3_bits plus_3_bits_1 (.in_1(in_1), .in_2(in_2), .q(plus_3_bits_1_q), .c(plus_3_bits_1_c[3]));
  bits_mod_5 bits_mod_5_1 (.in_1({plus_3_bits_1_c[3], plus_3_bits_1_q}), .out_2(out_3));
endmodule

module memory (
  input  reset,
  input  sync,
  input  [1:0] cmd,
  input  [2:0] index,
  input  [3:0] data,
  output [3:0] q0,
  output [3:0] q1,
  output [3:0] q2,
  output [3:0] q3,
  output [3:0] q4,
  output [3:0] Q
);

  wire and_1_out, and_2_out, and_3_out, and_4_out, and_5_out, and_6_out, and_7_out, not_1_out;
  wire [3:0] and_8_out, and_9_out, and_10_out, and_11_out, and_12_out, bit_extender_1_out,
       bit_extender_2_out, bit_extender_3_out, bit_extender_4_out, bit_extender_5_out;
  wire [7:0] dec_3_to_8_1_out_2;

  not not_1 (not_1_out, cmd[1]);
  and and_1 (and_1_out, cmd[0], not_1_out);
  and and_2 (and_2_out, sync, and_1_out);
  dec_3_to_8 dec_3_to_8_1 (.in_1(index), .out_2(dec_3_to_8_1_out_2));
  and and_3 (and_3_out, and_2_out, dec_3_to_8_1_out_2[0]);
  and and_4 (and_4_out, and_2_out, dec_3_to_8_1_out_2[1]);
  and and_5 (and_5_out, and_2_out, dec_3_to_8_1_out_2[2]);
  and and_6 (and_6_out, and_2_out, dec_3_to_8_1_out_2[3]);
  and and_7 (and_7_out, and_2_out, dec_3_to_8_1_out_2[4]);
  assign bit_extender_1_out = {{3{dec_3_to_8_1_out_2[0]}}, dec_3_to_8_1_out_2[0]};  // Bit_Extender bit_extender_1
  assign bit_extender_2_out = {{3{dec_3_to_8_1_out_2[1]}}, dec_3_to_8_1_out_2[1]};  // Bit_Extender bit_extender_2
  assign bit_extender_3_out = {{3{dec_3_to_8_1_out_2[2]}}, dec_3_to_8_1_out_2[2]};  // Bit_Extender bit_extender_3
  assign bit_extender_4_out = {{3{dec_3_to_8_1_out_2[3]}}, dec_3_to_8_1_out_2[3]};  // Bit_Extender bit_extender_4
  assign bit_extender_5_out = {{3{dec_3_to_8_1_out_2[4]}}, dec_3_to_8_1_out_2[4]};  // Bit_Extender bit_extender_5
  assign and_8_out = bit_extender_1_out & q0;  // AND_Gate and_8, 4 bits wide
  assign and_9_out = bit_extender_2_out & q1;  // AND_Gate and_9, 4 bits wide
  assign and_10_out = bit_extender_3_out & q2;  // AND_Gate and_10, 4 bits wide
  assign and_11_out = bit_extender_4_out & q3;  // AND_Gate and_11, 4 bits wide
  assign and_12_out = bit_extender_5_out & q4;  // AND_Gate and_12, 4 bits wide
  assign Q = and_8_out | and_9_out | and_10_out | and_11_out | and_12_out;  // OR_Gate or_1, 4 bits wide
  d_4_bits_trigger d_4_bits_trigger_1 (.reset(reset), .sync(and_3_out), .d(data), .q(q0));
  d_4_bits_trigger d_4_bits_trigger_2 (.reset(reset), .sync(and_4_out), .d(data), .q(q1));
  d_4_bits_trigger d_4_bits_trigger_3 (.reset(reset), .sync(and_5_out), .d(data), .q(q2));
  d_4_bits_trigger d_4_bits_trigger_4 (.reset(reset), .sync(and_6_out), .d(data), .q(q3));
  d_4_bits_trigger d_4_bits_trigger_5 (.reset(reset), .sync(and_7_out), .d(data), .q(q4));
endmodule

module stack (
  input  CLK,
  input  RESET,
  input  [1:0] COMMAND,
  input  [2:0] INDEX,
  input  [3:0] IO_DATA_in,
  output [3:0] d0,
  output [3:0] d1,
  output [3:0] d2,
  output [3:0] d3,
  output [3:0] d4,
  output [3:0] IO_DATA_out
);

  wire not_1_out, por_1_out, RESET_t;
  wire [1:0] and_1_out, bit_extender_1_out, CMD;
  wire [2:0] current_index_1_index, d_3_bits_trigger_1_q, shift_index_1_out_5;
  wire [3:0] DATA, memory_1_q;

  POR por_1 (.out(por_1_out));
  or or_1 (RESET_t, por_1_out, RESET);
  assign bit_extender_1_out = {{1{CLK}}, CLK};  // Bit_Extender bit_extender_1
  d_2_bits_trigger d_2_bits_trigger_1 (.reset(RESET_t), .sync(CLK), .d(COMMAND), .q(CMD));
  assign and_1_out = bit_extender_1_out & CMD;  // AND_Gate and_1, 2 bits wide
  current_index current_index_1 (.reset(RESET_t), .cmd(CMD), .sync(CLK), .index(current_index_1_index));
  not not_1 (not_1_out, CLK);
  inout_cmd inout_cmd_1 (.cmd(and_1_out), .pout(memory_1_q), .inpout(IO_DATA_in));
  shift_index shift_index_1 (
    .cmd(CMD), .sync(CLK), .curr_idx(current_index_1_index), .index(INDEX), .out_5(shift_index_1_out_5));
  d_3_bits_trigger d_3_bits_trigger_1 (.reset(RESET_t), .sync(CLK), .d(shift_index_1_out_5), .q(d_3_bits_trigger_1_q));
  d_4_bits_trigger d_4_bits_trigger_1 (.reset(RESET_t), .sync(CLK), .d(IO_DATA_in), .q(DATA));
  memory memory_1 (
    .reset(RESET_t), .sync(not_1_out), .cmd(CMD), .index(d_3_bits_trigger_1_q), .data(DATA), .q0(d4),
    .q1(d0), .q2(d1), .q3(d2), .q4(d3), .Q(memory_1_q));

  assign IO_DATA_out = IO_DATA_in;

  // Other names for the same wires on the sheet: cmd_t[1:0] = COMMAND; SYNC = CLK

  // Notes on the sheet:
  //   your circuit must be here
endmodule

module shift_index (
  input  [1:0] cmd,
  input  sync,
  input  [2:0] curr_idx,
  input  [2:0] index,
  output [2:0] out_5
);

  wire and_1_out, xor_1_out;
  wire [0:0] and_2_out;
  wire [2:0] and_3_out, bit_extender_1_out, bits_mod_5_1_out_2, next_index_1_next_idx;
  wire [3:0] neg_4_bits_1_out_2, plus_4_bits_1_q;

  assign bit_extender_1_out = {{2{and_1_out}}, and_1_out};  // Bit_Extender bit_extender_1
  and and_1 (and_1_out, cmd[0], sync, cmd[1]);
  xor xor_1 (xor_1_out, cmd[0], cmd[1]);
  bits_mod_5 bits_mod_5_1 (.in_1({1'b0, index}), .out_2(bits_mod_5_1_out_2));
  and and_2 (and_2_out[0], cmd[1], xor_1_out);
  next_index next_index_1 (.cmd({1'b0, and_2_out[0]}), .sync(sync), .index(curr_idx), .next_idx(next_index_1_next_idx));
  assign and_3_out = bit_extender_1_out & plus_4_bits_1_q[2:0];  // AND_Gate and_3, 3 bits wide
  plus_3_bits_mod_5 plus_3_bits_mod_5_1 (.in_1(next_index_1_next_idx), .in_2(and_3_out), .out_3(out_5));
  neg_4_bits neg_4_bits_1 (.in_1({1'b0, bits_mod_5_1_out_2}), .out_2(neg_4_bits_1_out_2));
  plus_4_bits plus_4_bits_1 (.in_1(neg_4_bits_1_out_2), .in_2(4'b0101), .q(plus_4_bits_1_q));  // open: c
endmodule

module next_index (
  input  [1:0] cmd,
  input  sync,
  input  [2:0] index,
  output [2:0] next_idx
);

  wire xor_1_out;
  wire [2:0] and_1_out;
  wire [3:0] and_3_out, bit_extender_1_out, plus_4_bits_1_q;

  xor xor_1 (xor_1_out, cmd[0], cmd[1]);
  assign bit_extender_1_out = {{3{sync}}, sync};  // Bit_Extender bit_extender_1
  and and_1 (and_1_out[0], cmd[0], xor_1_out);
  and and_2 (and_1_out[2], xor_1_out, cmd[1]);
  assign and_3_out = {1'b0, and_1_out[2], 1'b0, and_1_out[0]} & bit_extender_1_out;  // AND_Gate and_3, 4 bits wide
  plus_4_bits plus_4_bits_1 (.in_1(and_3_out), .in_2({1'b0, index}), .q(plus_4_bits_1_q));  // open: c
  bits_mod_5 bits_mod_5_1 (.in_1(plus_4_bits_1_q), .out_2(next_idx));
endmodule

module bits_mod_5 (
  input  [3:0] in_1,
  output [2:0] out_2
);

  wire is_more_5_1_out_2, is_more_10_1_out_2;
  wire [1:0] plus_5_bits_2_q;
  wire [4:0] and_1_out, and_2_out, bit_extender_1_out, bit_extender_2_out, bit_extender_3_out, neg_5, neg_10,
       plus_5_bits_1_q;

  assign bit_extender_1_out = {{1{1'b0}}, in_1};  // Bit_Extender bit_extender_1
  neg_5_bits neg_5_bits_1 (.in_1(5'b00101), .out_2(neg_5));
  neg_5_bits neg_5_bits_2 (.in_1(5'b01010), .out_2(neg_10));
  is_more_10 is_more_10_1 (.in_1(bit_extender_1_out), .out_2(is_more_10_1_out_2));
  is_more_5 is_more_5_1 (.in_1(plus_5_bits_1_q), .out_2(is_more_5_1_out_2));
  assign bit_extender_2_out = {{4{is_more_10_1_out_2}}, is_more_10_1_out_2};  // Bit_Extender bit_extender_2
  assign bit_extender_3_out = {{4{is_more_5_1_out_2}}, is_more_5_1_out_2};  // Bit_Extender bit_extender_3
  assign and_1_out = bit_extender_2_out & neg_10;  // AND_Gate and_1, 5 bits wide
  assign and_2_out = bit_extender_3_out & neg_5;  // AND_Gate and_2, 5 bits wide
  plus_5_bits plus_5_bits_1 (.in_1(bit_extender_1_out), .in_2(and_1_out), .q(plus_5_bits_1_q));  // open: c
  plus_5_bits plus_5_bits_2 (.in_1(plus_5_bits_1_q), .in_2(and_2_out), .q({plus_5_bits_2_q, out_2}));  // open: c
endmodule

module plus_4_bits (
  input  [3:0] in_1,
  input  [3:0] in_2,
  output [3:0] q,
  output c
);

  wire plus_3_bits_1_c;

  plus_3_bits plus_3_bits_1 (.in_1(in_1[2:0]), .in_2(in_2[2:0]), .q(q[2:0]), .c(plus_3_bits_1_c));
  plus3 plus3_1 (.in_1(plus_3_bits_1_c), .in_2(in_1[3]), .in_3(in_2[3]), .s(q[3]), .c(c));
endmodule

module plus_5_bits (
  input  [4:0] in_1,
  input  [4:0] in_2,
  output [4:0] q,
  output c
);

  wire plus_4_bits_1_c;

  plus_4_bits plus_4_bits_1 (.in_1(in_1[3:0]), .in_2(in_2[3:0]), .q(q[3:0]), .c(plus_4_bits_1_c));
  plus3 plus3_1 (.in_1(plus_4_bits_1_c), .in_2(in_1[4]), .in_3(in_2[4]), .s(q[4]), .c(c));
endmodule

module inout_cmd (
  input  [1:0] cmd,
  input  [3:0] pout,
  output [3:0] inpout
);

  wire not_1_out;

  Transistor #(.\type ("n"), .width(4)) transistor_1 (.in(pout), .out(inpout), .gate(cmd[1]));
  not not_1 (not_1_out, cmd[1]);
  Transistor #(.width(4)) transistor_2 (.in(pout), .out(inpout), .gate(not_1_out));
endmodule

module d_2_bits_trigger (
  input  reset,
  input  sync,
  input  [1:0] d,
  output [1:0] q
);

  wire d0, d1, d_trigger_1_neg_q, d_trigger_2_neg_q, not_1_out, SYNC_t;
  wire [1:0] bit_extender_1_out;

  not not_1 (not_1_out, reset);
  assign bit_extender_1_out = {{1{not_1_out}}, not_1_out};  // Bit_Extender bit_extender_1
  assign {d1, d0} = bit_extender_1_out & d;  // AND_Gate and_1, 2 bits wide
  or or_1 (SYNC_t, reset, sync);
  d_trigger d_trigger_1 (.d(d0), .c(SYNC_t), .q(q[0]), .neg_q(d_trigger_1_neg_q));
  d_trigger d_trigger_2 (.d(d1), .c(SYNC_t), .q(q[1]), .neg_q(d_trigger_2_neg_q));
endmodule

module neg_4_bits (
  input  [3:0] in_1,
  output [3:0] out_2
);

  wire [3:0] not_1_out;

  assign not_1_out = ~in_1;  // NOT_Gate not_1, 4 bits wide
  plus_4_bits plus_4_bits_1 (.in_1(not_1_out), .in_2(4'b0001), .q(out_2));  // open: c
endmodule

module is_more_5 (
  input  [4:0] in_1,
  output out_2
);

  wire [4:0] neg_5, plus_5_bits_1_q;

  neg_5_bits neg_5_bits_1 (.in_1(5'b00101), .out_2(neg_5));
  plus_5_bits plus_5_bits_1 (.in_1(in_1), .in_2(neg_5), .q(plus_5_bits_1_q));  // open: c
  not not_1 (out_2, plus_5_bits_1_q[4]);
endmodule

module neg_5_bits (
  input  [4:0] in_1,
  output [4:0] out_2
);

  wire [4:0] not_1_out;

  assign not_1_out = ~in_1;  // NOT_Gate not_1, 5 bits wide
  plus_5_bits plus_5_bits_1 (.in_1(not_1_out), .in_2(5'b00001), .q(out_2));  // open: c
endmodule

module is_more_10 (
  input  [4:0] in_1,
  output out_2
);

  wire [4:0] neg_10, plus_5_bits_1_q;

  neg_5_bits neg_5_bits_1 (.in_1(5'b01010), .out_2(neg_10));
  plus_5_bits plus_5_bits_1 (.in_1(in_1), .in_2(neg_10), .q(plus_5_bits_1_q));  // open: c
  not not_1 (out_2, plus_5_bits_1_q[4]);
endmodule
